# Fritzing sketch tasercraft (saved by Fritzing 0.9.4)
circuit board: 8.25cm x 5.65cm
breadboards: 2

parts:
  Arduino_Nano = Arduino Nano (Rev3.0)
  LED2 = LED - 5mm [color="Green (560nm)" package="5 mm [THT]"]
  LED1 = LED - 5mm [color="Yellow (585nm)" package="5 mm [THT]"]
  LED3 = LED - 5mm [color="Red (633nm)" package="5 mm [THT]"]
  R3 = Resistor [tolerance=±5% resistance=220 package=THT]
  R1 = Resistor [tolerance=±5% resistance=220 package=THT]
  R2 = Resistor [tolerance=±5% resistance=220 package=THT]
  XL6009 = RioRand LM2596
  VREG_POT = IC, SIP package, 3 pins [chip_label="potentiometer in"]
  MCP4131 = IC, DIP package, 8 pins [chip_label=MCP4131]
  R4 = Resistor [tolerance=±5% resistance=220 package=THT]
  COIL = Transformer [package=transformer]
  RELAY = RELAY [package=relay-g5q]
  C1 = Ceramic Capacitor [capacitance=10µF voltage=50V package="100 mil [THT, multilayer]"]
  S1 = Toggle Switch [package=THT]
  J2 = XT60 Connector [package=THT]
  5V_REG = Mini-360 DC-DC Buck converter [package=THT]
  buz1 = Piezo Buzzer

nets:
  GND: Arduino_Nano.GND, LED2.cathode, LED1.cathode, LED3.cathode, XL6009.Pin_2, XL6009.Pin_4, MCP4131.pin4, COIL.2, RELAY.COIL2, C1.1, J2.GND, 5V_REG.IN-, 5V_REG.OUT-, buz1.pin_1
  N1: Arduino_Nano.D5, RELAY.COIL1
  N2: Arduino_Nano.D7, buz1.pin_2
  N3: Arduino_Nano.D8, R1.Pin_0
  N4: Arduino_Nano.D9, R2.Pin_0
  N5: Arduino_Nano.D10, MCP4131.pin1
  N6: Arduino_Nano.D11/MOSI, R4.Pin_1
  N7: Arduino_Nano.D12/MISO, MCP4131.pin3, R4.Pin_0
  N8: Arduino_Nano.5V, R3.Pin_0, MCP4131.pin8, 5V_REG.OUT+
  N9: Arduino_Nano.D13/SCK, MCP4131.pin2
  N10: LED2.anode, R2.Pin_1
  N11: LED1.anode, R1.Pin_1
  N12: LED3.anode, R3.Pin_1
  N13: XL6009.Pin_1, S1.L1, 5V_REG.IN+
  N14: XL6009.Pin_3, RELAY.MAIN
  N15: VREG_POT.pin1, MCP4131.pin5
  N16: VREG_POT.pin2, MCP4131.pin6
  N17: VREG_POT.pin3, MCP4131.pin7
  N18: COIL.1, RELAY.NO, C1.0
  N19: S1.COM, J2.VCC

custom parts:
  XT60 Connector: Yellow XT60 connector for high current loads up to 40A
  Mini-360 DC-DC Buck converter: Mini-360 DC-DC Buck converter. Tiny buck step down voltage converter, input voltage 4.75 to 23V output 1 to 17V adjustable. Available from ebay and the like.
  Piezo Buzzer: Part from https://www.nutsvolts.com/magazine/article/november2012_SmileysWorkshop modified to be .3 in spacing to match the adafruit buzzer 5V breadboard friendly part.
